# Fritzing sketch instrumentation2aop (saved by Fritzing 0.9.3b)
breadboards: 1

parts:
  R5 = Resistor [tolerance=±5% resistance=56k package="2010 [SMD]"]
  U3 = LM386 [package=dip08]
  R6 = Resistor [tolerance=±5% resistance=1k package="2010 [SMD]"]
  R7 = Resistor [tolerance=±5% resistance=1k package="2010 [SMD]"]
  R8 = Resistor [tolerance=±5% resistance=56k package="2010 [SMD]"]
  U4 = LM386 [package=dip08]
  U5 = TOUCH [package=touch2]

nets:
  N1: R5.Pin_1, U3.-IN, R6.Pin_0
  N2: U3.+IN, U5.T1
  N3: U3.V-, U4.V-
  N4: U3.V+, R6.Pin_1, R7.Pin_0
  N5: U3.BP, U4.BP
  N6: R7.Pin_1, R8.Pin_0, U4.-IN
  N7: R8.Pin_1, U4.V+
  N8: U4.+IN, U5.T2

// code stored in the sketch: Untitled3.ino

