# Fritzing sketch instrumentation3aop (saved by Fritzing 0.9.3b)
breadboards: 1

parts:
  R3 = Resistor [tolerance=±5% resistance=4.7k package="2010 [SMD]"]
  U2 = LM386 [package=dip08]
  U3 = LM386 [package=dip08]
  R4 = Resistor [tolerance=±5% resistance=1k package="2010 [SMD]"]
  R5 = Resistor [tolerance=±5% resistance=4.7k package="2010 [SMD]"]
  R6 = Resistor [tolerance=±5% resistance=4.7k package="2010 [SMD]"]
  U4 = LM386 [package=dip08]
  R7 = Resistor [tolerance=±5% resistance=4.7k package="2010 [SMD]"]
  R8 = Resistor [tolerance=±5% resistance=4.7k package="2010 [SMD]"]
  R9 = Resistor [tolerance=±5% resistance=4.7k package="2010 [SMD]"]

nets:
  N1: R3.Pin_0, U2.V+, R5.Pin_1
  N2: R3.Pin_1, R6.Pin_0, U4.-IN
  N3: U2.-IN, R4.Pin_1, R5.Pin_0
  N4: U2.V-, U3.V-, U4.V-
  N5: U2.BP, U3.BP, U4.BP
  N6: U3.-IN, R4.Pin_0, R7.Pin_1
  N7: U3.V+, R7.Pin_0, R8.Pin_1
  N8: R6.Pin_1, U4.V+
  N9: R8.Pin_0, R9.Pin_1
