# Fritzing sketch suiveurnoninverseur (saved by Fritzing 0.9.3b)
breadboards: 1

parts:
  U3 = LM386 [package=dip08]
  U5 = TOUCH [package=touch2]
  U6 = LM386 [package=dip08]
  R1 = Resistor [tolerance=±5% resistance=130k package="2010 [SMD]"]
  R2 = Resistor [tolerance=±5% resistance=1k package="2010 [SMD]"]
  C1 = Tantalum Capacitor [capacitance=1μF package="100 mil [THT, tantalum]"]

nets:
  N1: U3.-IN, U3.V+, U6.+IN
  N2: U3.+IN, U5.T2
  N3: U3.V-, U6.V-
  N4: U3.BP, U6.BP
  N5: U5.T1, R2.Pin_1
  N6: U6.-IN, R1.Pin_1, R2.Pin_0
  N7: U6.V+, R1.Pin_0, C1.-

// code stored in the sketch: Untitled3.ino

